# Fritzing sketch 数字密码锁 (saved by Fritzing 0.9.3b)
breadboards: 1

parts:
  IC1 = IC, DIP package, 14 pins [chip_label=74HC00]
  IC2 = IC, DIP package, 14 pins [chip_label=74HC20]
  IC3 = IC, DIP package, 14 pins [chip_label=74HC00]

nets:
  N1: IC1.pin1, IC1.pin2
  N2: IC1.pin3, IC2.pin2
  N3: IC1.pin4, IC1.pin5
  N4: IC1.pin6, IC2.pin4
  N5: IC1.pin7, IC2.pin7, IC3.pin7
  N6: IC1.pin8, IC3.pin12, IC3.pin13
  N7: IC1.pin9, IC3.pin1
  N8: IC1.pin10, IC1.pin12, IC1.pin13, IC2.pin6
  N9: IC1.pin11, IC3.pin2
  N10: IC1.pin14, IC2.pin14, IC3.pin14
  N11: IC3.pin3, IC3.pin9, IC3.pin10
