# Fritzing sketch 一位全加器 (saved by Fritzing 0.9.3b)
breadboards: 1

parts:
  IC1 = IC, DIP package, 16 pins [chip_label=74HC138]
  IC4 = IC, DIP package, 14 pins [chip_label=74HC20]

nets:
  N1: IC1.pin4, IC1.pin5, IC1.pin8, IC4.pin7
  N2: IC1.pin7, IC4.pin4, IC4.pin9
  N3: IC1.pin9, IC4.pin5
  N4: IC1.pin10, IC4.pin2
  N5: IC1.pin11, IC4.pin10
  N6: IC1.pin12, IC4.pin1
  N7: IC1.pin13, IC4.pin12
  N8: IC1.pin14, IC4.pin13
  N9: IC1.pin16, IC4.pin14
