# Fritzing sketch 原码转补码（74138） (saved by Fritzing 0.9.3b)
breadboards: 1

parts:
  IC1 = IC, DIP package, 16 pins [chip_label=74HC138]
  IC2 = IC, DIP package, 14 pins [chip_label=74HC20]

nets:
  N1: IC1.pin4, IC1.pin5, IC1.pin8, IC2.pin7
  N2: IC1.pin9, IC2.pin2
  N3: IC1.pin10, IC2.pin1
  N4: IC1.pin11, IC2.pin12
  N5: IC1.pin12, IC2.pin13
  N6: IC1.pin13, IC2.pin4, IC2.pin10
  N7: IC1.pin14, IC2.pin5, IC2.pin9
  N8: IC1.pin16, IC2.pin14
