# Fritzing sketch 原码转补码（74151） (saved by Fritzing 0.9.3b)
breadboards: 1

parts:
  IC1 = IC, DIP package, 16 pins [chip_label=74HC151]
  IC2 = IC, DIP package, 16 pins [chip_label=74HC151]

nets:
  N1: IC1.pin1, IC1.pin2, IC1.pin3, IC2.pin2, IC2.pin3
  N2: IC1.pin4, IC1.pin7, IC1.pin8, IC2.pin1, IC2.pin4, IC2.pin7, IC2.pin8
  N3: IC1.pin9, IC2.pin9
  N4: IC1.pin10, IC2.pin10
  N5: IC1.pin11, IC2.pin11
  N6: IC1.pin12, IC1.pin13, IC1.pin14, IC2.pin12, IC2.pin15
  N7: IC1.pin15, IC1.pin16, IC2.pin13, IC2.pin14, IC2.pin16
