# Fritzing sketch 原码转补码（门电路） (saved by Fritzing 0.9.3b)
breadboards: 1

parts:
  IC1 = IC, DIP package, 14 pins [chip_label=74HC00]
  IC2 = IC, DIP package, 14 pins [chip_label=74HC86]

nets:
  N1: IC1.pin1, IC1.pin2, IC2.pin4
  N2: IC1.pin3, IC1.pin13
  N3: IC1.pin4, IC1.pin5, IC2.pin5
  N4: IC1.pin6, IC1.pin12
  N5: IC1.pin7, IC2.pin7
  N6: IC1.pin11, IC2.pin1
  N7: IC1.pin14, IC2.pin14
