# Fritzing sketch 发电机控制器 (saved by Fritzing 0.9.3b)
breadboards: 1

parts:
  IC1 = IC, DIP package, 16 pins [chip_label=74HC138]
  IC2 = IC, DIP package, 14 pins [chip_label=74HC00]
  IC3 = IC, DIP package, 14 pins [chip_label=74HC20]

nets:
  N1: IC1.pin1, IC2.pin1, IC2.pin2
  N2: IC1.pin4, IC1.pin5, IC1.pin8, IC2.pin7, IC3.pin7
  N3: IC1.pin7, IC3.pin13
  N4: IC1.pin9, IC2.pin13
  N5: IC1.pin11, IC3.pin12
  N6: IC1.pin12, IC3.pin10
  N7: IC1.pin13, IC3.pin9
  N8: IC1.pin16, IC2.pin14, IC3.pin14
  N9: IC2.pin3, IC2.pin12
