# Fritzing sketch 血型配对 (saved by Fritzing 0.9.3b)
breadboards: 1

parts:
  IC1 = IC, DIP package, 16 pins [chip_label=74HC151]
  IC2 = IC, DIP package, 14 pins [chip_label=74HC00]

nets:
  N1: IC1.pin1, IC1.pin3, IC2.pin14
  N2: IC1.pin2, IC1.pin4, IC1.pin13, IC2.pin3
  N3: IC1.pin7, IC1.pin8
  N4: IC1.pin12, IC1.pin16
  N5: IC1.pin14, IC1.pin15, IC2.pin7
  N6: IC2.pin1, IC2.pin2
