# Fritzing sketch 广告流水灯 (saved by Fritzing 0.9.3b)
breadboards: 1

parts:
  IC1 = IC, DIP package, 14 pins [chip_label=74HC74]
  IC2 = IC, DIP package, 14 pins [chip_label=74HC74]
  IC3 = IC, DIP package, 16 pins [chip_label=74HC138]

nets:
  N1: IC1.pin1, IC1.pin4, IC2.pin1, IC2.pin4, IC3.pin6
  N2: IC1.pin2, IC1.pin6, IC1.pin11
  N3: IC1.pin5, IC3.pin1
  N4: IC1.pin7, IC2.pin7, IC3.pin4, IC3.pin5, IC3.pin8
  N5: IC1.pin8, IC1.pin12, IC2.pin3
  N6: IC1.pin9, IC3.pin2
  N7: IC1.pin10, IC1.pin13, IC1.pin14, IC2.pin14, IC3.pin16
  N8: IC2.pin2, IC2.pin6
  N9: IC2.pin5, IC3.pin3
