# Fritzing sketch 序列发生器 (saved by Fritzing 0.9.3b)
breadboards: 1

parts:
  IC1 = IC, DIP package, 16 pins [chip_label=74HC161]
  IC2 = IC, DIP package, 14 pins [chip_label=74HC00]

nets:
  N1: IC1.pin1, IC1.pin3, IC1.pin4, IC1.pin6, IC1.pin7
  N2: IC1.pin5, IC1.pin8, IC2.pin7
  N3: IC1.pin9, IC2.pin11
  N4: IC1.pin10, IC1.pin16, IC2.pin14
  N5: IC1.pin15, IC2.pin12, IC2.pin13
