# Fritzing sketch 曼切斯特编码(不使用74194) (saved by Fritzing 0.9.3b)
breadboards: 1

parts:
  IC1 = IC, DIP package, 16 pins [chip_label=74HC161]
  IC2 = IC, DIP package, 16 pins [chip_label=74HC161]
  IC3 = IC, DIP package, 16 pins [chip_label=74HC151]
  IC4 = IC, DIP package, 14 pins [chip_label=74HC00]
  IC5 = IC, DIP package, 14 pins [chip_label=74HC86]

nets:
  N1: IC1.pin1, IC1.pin7, IC2.pin1
  N2: IC1.pin3, IC1.pin4, IC1.pin5, IC1.pin6, IC1.pin8, IC2.pin7, IC2.pin8, IC3.pin7, IC3.pin8, IC4.pin7, IC5.pin7
  N3: IC1.pin9, IC2.pin9, IC4.pin11
  N4: IC1.pin10, IC1.pin16, IC2.pin10, IC2.pin16, IC3.pin16, IC4.pin14, IC5.pin14
  N5: IC1.pin12, IC3.pin9
  N6: IC1.pin13, IC3.pin10, IC4.pin12
  N7: IC1.pin14, IC3.pin11, IC4.pin13
  N8: IC2.pin2, IC5.pin2
  N9: IC2.pin11, IC3.pin4
  N10: IC2.pin12, IC3.pin3
  N11: IC2.pin13, IC3.pin2
  N12: IC2.pin14, IC3.pin1
  N13: IC3.pin5, IC5.pin1
