# Fritzing sketch 曼切斯特编码 (saved by Fritzing 0.9.3b)
breadboards: 1

parts:
  IC1 = IC, DIP package, 14 pins [chip_label=74HC00]
  IC2 = IC, DIP package, 14 pins [chip_label=74HC86]
  IC3 = IC, DIP package, 16 pins [chip_label=74HC194]
  IC4 = IC, DIP package, 16 pins [chip_label=74HC161]

nets:
  N1: IC1.pin7, IC2.pin7, IC3.pin2, IC3.pin7, IC3.pin8, IC4.pin3, IC4.pin4, IC4.pin5, IC4.pin6, IC4.pin8
  N2: IC1.pin8, IC3.pin10
  N3: IC1.pin9, IC1.pin10, IC1.pin11, IC4.pin9
  N4: IC1.pin12, IC4.pin13
  N5: IC1.pin13, IC4.pin14
  N6: IC1.pin14, IC2.pin14, IC3.pin9, IC3.pin16, IC4.pin10, IC4.pin16
  N7: IC2.pin12, IC3.pin11
  N8: IC2.pin13, IC3.pin12
  N9: IC3.pin1, IC4.pin1, IC4.pin7
